# Fritzing sketch solenoid_control (saved by Fritzing 0.9.5d)

parts:
  L298N1 = L298N motor driver
  Part1 = Arduino Uno (Rev3) - ICSP
  L3 = Inductor [package="1206 [SMD]"]  # not connected
  L4 = Inductor [package="0805 [SMD]"]  # not connected
  J1 = female pin header, 2 pins [form="♀ (female)"]  # not connected
  J2 = female pin header, 2 pins [form="♀ (female)"]  # not connected

nets:
  N1: L298N1.connector13, Part1.D8
  N2: L298N1.connector14, Part1.D9_PWM
  N3: L298N1.connector15, Part1.D10_PWM/SS
  N4: L298N1.connector16, Part1.D11_PWM/MOSI
